# Fritzing sketch 3x3x3 (saved by Fritzing 0.8.6b)
circuit board: 8.46667cm x 5.64444cm

parts:
  LED19 = LED - 3mm [color="Blue (430nm)" package="3 mm [THT]"]
  LED20 = LED - 3mm [color="Blue (430nm)" package="3 mm [THT]"]
  LED21 = LED - 3mm [color="Blue (430nm)" package="3 mm [THT]"]
  LED22 = LED - 3mm [color="Blue (430nm)" package="3 mm [THT]"]
  LED23 = LED - 3mm [color="Blue (430nm)" package="3 mm [THT]"]
  LED24 = LED - 3mm [color="Blue (430nm)" package="3 mm [THT]"]
  LED25 = LED - 3mm [color="Blue (430nm)" package="3 mm [THT]"]
  LED26 = LED - 3mm [color="Blue (430nm)" package="3 mm [THT]"]
  LED27 = LED - 3mm [color="Blue (430nm)" package="3 mm [THT]"]
  R1 = Resistor [tolerance=±5% resistance=220 package=THT]
  R2 = Resistor [tolerance=±5% resistance=220 package=THT]
  R3 = Resistor [tolerance=±5% resistance=220 package=THT]
  R4 = Resistor [tolerance=±5% resistance=220 package=THT]
  R5 = Resistor [tolerance=±5% resistance=220 package=THT]
  R6 = Resistor [tolerance=±5% resistance=220 package=THT]
  R7 = Resistor [tolerance=±5% resistance=220 package=THT]
  R8 = Resistor [tolerance=±5% resistance=220 package=THT]
  R9 = Resistor [tolerance=±5% resistance=220 package=THT]
  Q1 = NPN-Transistor [package="TO92 [THT]"]
  Componente1 = Arduino Pro Mini v13
  R10 = Resistor [tolerance=±5% resistance=4.7k package=THT]

nets:
  N1: LED19.cathode, R7.Pin_1
  N2: LED19.anode, LED20.anode, LED21.anode, LED22.anode, LED23.anode, LED24.anode, LED25.anode, LED26.anode, LED27.anode, Q1.E
  N3: LED20.cathode, R4.Pin_1
  N4: LED21.cathode, R6.Pin_1
  N5: LED22.cathode, R3.Pin_1
  N6: LED23.cathode, R2.Pin_1
  N7: LED24.cathode, R1.Pin_1
  N8: LED25.cathode, R9.Pin_1
  N9: LED26.cathode, R8.Pin_1
  N10: LED27.cathode, R5.Pin_1
  N11: R1.Pin_0, Componente1.D8
  N12: R2.Pin_0, Componente1.D7
  N13: R3.Pin_0, Componente1.D6_PWM
  N14: R4.Pin_0, Componente1.D5_PWM
  N15: R5.Pin_0, Componente1.D3_PWM
  N16: R6.Pin_0, Componente1.D2
  N17: R7.Pin_0, Componente1.A0
  N18: R8.Pin_0, Componente1.D13/SCK
  N19: R9.Pin_0, Componente1.D12/MISO
  N20: Q1.B, R10.Pin_1
  N21: Q1.C, Componente1.GND
  N22: Componente1.D9_PWM, R10.Pin_0
