# Fritzing sketch 9x9x9 (saved by Fritzing 0.8.6b)
breadboards: 1

parts:
  U1 = 74HC595 [package="DIP16 [THT]"]
  LED1 = LED - 5mm [color="Blue (470nm)" package="5 mm [THT]"]
  LED2 = LED - 5mm [color="Blue (470nm)" package="5 mm [THT]"]
  LED3 = LED - 5mm [color="Blue (470nm)" package="5 mm [THT]"]
  LED4 = LED - 5mm [color="Blue (470nm)" package="5 mm [THT]"]
  LED5 = LED - 5mm [color="Blue (470nm)" package="5 mm [THT]"]
  LED6 = LED - 5mm [color="Blue (470nm)" package="5 mm [THT]"]
  LED7 = LED - 5mm [color="Blue (470nm)" package="5 mm [THT]"]
  LED8 = LED - 5mm [color="Blue (470nm)" package="5 mm [THT]"]  # not connected
  LED9 = LED - 5mm [color="Blue (470nm)" package="5 mm [THT]"]  # not connected

nets:
  N1: U1.Q1, LED2.anode
  N2: U1.Q2, LED3.anode
  N3: U1.Q3, LED4.anode
  N4: U1.Q4, LED5.anode
  N5: U1.Q5, LED6.anode
  N6: U1.Q6, LED7.anode
  N7: U1.Q0, LED1.anode
