# Fritzing sketch max7219 (saved by Fritzing 0.8.7b)
breadboards: 2

parts:
  U1 = MAX7219 [package=dil24]
  R1 = Resistor [tolerance=±5% resistance=22k package=THT]
  C1 = Ceramic Capacitor [capacitance=100nF package="100 mil [THT, multilayer]"]
  U2 = MAX7219 [package=dil24]
  R2 = Resistor [tolerance=±5% resistance=22k package=THT]
  C2 = Ceramic Capacitor [capacitance=100nF package="100 mil [THT, multilayer]"]
  LED1 = LED - 5mm [color="Red (633nm)" package="5 mm [THT]"]
  LED2 = LED - 5mm [color="Red (633nm)" package="5 mm [THT]"]
  LED3 = LED - 5mm [color="Red (633nm)" package="5 mm [THT]"]
  LED4 = LED - 5mm [color="Red (633nm)" package="5 mm [THT]"]
  LED5 = LED - 5mm [color="Red (633nm)" package="5 mm [THT]"]
  LED6 = LED - 5mm [color="Red (633nm)" package="5 mm [THT]"]
  LED7 = LED - 5mm [color="Red (633nm)" package="5 mm [THT]"]
  LED8 = LED - 5mm [color="Red (633nm)" package="5 mm [THT]"]
  LED9 = LED - 5mm [color="Red (633nm)" package="5 mm [THT]"]
  LED10 = LED - 5mm [color="Red (633nm)" package="5 mm [THT]"]
  LED11 = LED - 5mm [color="Red (633nm)" package="5 mm [THT]"]
  LED12 = LED - 5mm [color="Red (633nm)" package="5 mm [THT]"]
  LED13 = LED - 5mm [color="Red (633nm)" package="5 mm [THT]"]
  LED14 = LED - 5mm [color="Red (633nm)" package="5 mm [THT]"]
  LED15 = LED - 5mm [color="Red (633nm)" package="5 mm [THT]"]
  LED16 = LED - 5mm [color="Red (633nm)" package="5 mm [THT]"]
  LED17 = LED - 5mm [color="Red (633nm)" package="5 mm [THT]"]
  LED18 = LED - 5mm [color="Red (633nm)" package="5 mm [THT]"]
  LED19 = LED - 5mm [color="Red (633nm)" package="5 mm [THT]"]
  LED20 = LED - 5mm [color="Red (633nm)" package="5 mm [THT]"]
  LED21 = LED - 5mm [color="Red (633nm)" package="5 mm [THT]"]
  LED22 = LED - 5mm [color="Red (633nm)" package="5 mm [THT]"]
  LED23 = LED - 5mm [color="Red (633nm)" package="5 mm [THT]"]
  LED24 = LED - 5mm [color="Red (633nm)" package="5 mm [THT]"]
  LED25 = LED - 5mm [color="Red (633nm)" package="5 mm [THT]"]
  LED26 = LED - 5mm [color="Red (633nm)" package="5 mm [THT]"]
  LED27 = LED - 5mm [color="Red (633nm)" package="5 mm [THT]"]
  LED28 = LED - 5mm [color="Red (633nm)" package="5 mm [THT]"]
  LED29 = LED - 5mm [color="Red (633nm)" package="5 mm [THT]"]
  LED30 = LED - 5mm [color="Red (633nm)" package="5 mm [THT]"]
  LED31 = LED - 5mm [color="Red (633nm)" package="5 mm [THT]"]
  LED32 = LED - 5mm [color="Red (633nm)" package="5 mm [THT]"]

nets:
  N1: U1.DIN, U2.DOUT
  N2: U1.DIG0, LED3.anode, LED22.anode
  N3: U1.DIG4, LED4.anode, LED23.anode
  GND: U1.GND, U1.GND2, C2.0
  N4: U1.DIG6, U1.SEGA, U2.DIG2, U2.DIG3, U2.SEGA, LED15.anode, LED17.cathode, LED18.cathode, LED19.cathode, LED20.cathode, LED20.anode, LED21.cathode, LED22.cathode, LED23.cathode, LED24.cathode, LED24.anode, LED25.cathode, LED26.cathode, LED27.cathode, LED28.cathode, LED29.cathode, LED30.cathode, LED31.cathode, LED32.cathode
  N5: U1.DIG2, LED9.anode, LED26.anode
  N6: U1.DIG3, LED13.anode, LED29.anode
  N7: U1.DIG7, LED16.anode, LED31.anode
  N8: U1.DIG5, LED8.anode, LED17.anode
  N9: U1.DIG1, LED5.anode, LED19.anode
  N10: U1.SEGB, LED1.cathode, LED2.cathode, LED3.cathode, LED4.cathode, LED5.cathode, LED6.cathode, LED7.cathode, LED8.cathode, LED9.cathode, LED10.cathode, LED11.cathode, LED12.cathode, LED13.cathode, LED14.cathode, LED15.cathode, LED16.cathode
  N11: U1.ISET, R1.Pin_1
  N12: U1.VCC, R1.Pin_0, C1.1
  N13: U2.DIG0, LED1.anode, LED32.anode
  N14: U2.DIG4, LED2.anode, LED28.anode
  GND_2: U2.GND, U2.GND2
  N15: U2.DIG6, LED10.anode, LED30.anode
  N16: U2.DIG7, LED14.anode, LED18.anode
  N17: U2.DIG5, LED6.anode, LED25.anode
  N18: U2.DIG1, LED7.anode, LED27.anode
  N19: U2.ISET, R2.Pin_1
  N20: U2.VCC, R2.Pin_0, C2.1
  N21: LED12.anode, LED21.anode

notes:
  Digit = sink 320mA = cathode
  Segment = source 40mA = anode
  Rset = 22k blue, 28k red
  Led cathode (-) is short leg
